// Logisim project processor.circ as structural Verilog: 17 circuits, main circuit main
module main (
  input  reset
);

  wire alu_1_eqz, alu_1_gt, and_1_out, and_2_out, clock_1_out, CONTROL_beqz, CONTROL_bgt, CONTROL_dm_alu,
       CONTROL_input, CONTROL_j_jal, CONTROL_jal, CONTROL_jr, CONTROL_output, CONTROL_rt_imm, CONTROL_rt_rd,
       CONTROL_sw, CONTROL_we, keyboard_1_avail, not_1_out, not_2_out, or_1_out, type_1_out_2;
  wire [2:0] multiplexer_3_out, multiplexer_4_out, multiplexer_5_out, multiplexer_6_out, rom_1_data,
       rom_1_data_4;
  wire [5:3] rom_1_data_2;
  wire [6:0] keyboard_1_data;
  wire [15:0] alu_1_outputdata, inputto16_1_out, multiplexer_1_out, multiplexer_2_out, multiplexer_7_out,
       multiplexer_8_out, multiplexer_9_out, multiplexer_10_out, multiplexer_11_out, n16add_1_out_4, PC_out,
       plus_1_out_4, ram_1_data, regfile_1_rs, regfile_1_rt, SX_out_2, top4pc_1_newpc;
  wire [15:6] rom_1_data_3;

  _16bitregister PC (
    .write_enable(1'b1), .clock(clock_1_out), .in(multiplexer_11_out), .reset_input(reset), .out(PC_out));
  Keyboard keyboard_1 (
    .clk(clock_1_out), .re(CONTROL_input), .clr(reset), .avail(keyboard_1_avail), .data(keyboard_1_data));
  \type  type_1 (.in_1(rom_1_data_3[15:12]), .out_2(type_1_out_2));  // open: out_3, out_4
  _16add plus_1 (.sub(1'b0), .in_2(16'h1), .in_3(PC_out), .out_4(plus_1_out_4));  // open: cOUt, ovf
  inputTo16 inputto16_1 (.in_1(keyboard_1_data), .valid(keyboard_1_avail), .out(inputto16_1_out));
  ROM #(.addrWidth(16), .dataWidth(16)) rom_1 (
    .addr(PC_out), .data({rom_1_data_3[15:12], rom_1_data_4, rom_1_data_3[8:6], rom_1_data_2, rom_1_data}));  // open: sel
  Multiplexer #(.width(16)) multiplexer_1 (
    .in0(multiplexer_10_out), .in1(plus_1_out_4), .out(multiplexer_1_out), .sel(CONTROL_jal));  // open: en
  Control CONTROL (
    .opcode(rom_1_data_3[15:12]), .jal(CONTROL_jal), .\input (CONTROL_input), .WE(CONTROL_we),
    .rt_rd(CONTROL_rt_rd), .rt_imm(CONTROL_rt_imm), .beqz(CONTROL_beqz), .sw(CONTROL_sw),
    .j_jal(CONTROL_j_jal), .jr(CONTROL_jr), .DM_ALU(CONTROL_dm_alu), .\output (CONTROL_output),
    .bgt(CONTROL_bgt));
  Multiplexer #(.width(16)) multiplexer_2 (
    .in0(multiplexer_1_out), .in1(inputto16_1_out), .out(multiplexer_2_out), .sel(CONTROL_input));  // open: en
  Multiplexer #(.width(3)) multiplexer_3 (
    .in0(rom_1_data_4), .in1(rom_1_data_4), .out(multiplexer_3_out), .sel(type_1_out_2));  // open: en
  Clock clock_1 (.out(clock_1_out));
  not not_1 (not_1_out, clock_1_out);
  Multiplexer #(.width(3)) multiplexer_4 (
    .in0(rom_1_data_2), .in1(multiplexer_5_out), .out(multiplexer_4_out), .sel(CONTROL_rt_rd));  // open: en
  Multiplexer #(.width(3)) multiplexer_5 (
    .in0(rom_1_data_3[8:6]), .in1(rom_1_data_3[8:6]), .out(multiplexer_5_out), .sel(type_1_out_2));  // open: en
  regfile regfile_1 (
    .clock(not_1_out), .rsReg(multiplexer_3_out), .RegWriteEnable(CONTROL_we), .rdReg(multiplexer_6_out),
    .writeData(multiplexer_2_out), .rs(regfile_1_rs), .rt(regfile_1_rt), .rtReg(multiplexer_5_out),
    .global_reset(reset));
  Multiplexer #(.width(3)) multiplexer_6 (
    .in0(multiplexer_4_out), .in1(3'b111), .out(multiplexer_6_out), .sel(CONTROL_jal));  // open: en
  sign_extender SX (.in_1({rom_1_data_2, rom_1_data}), .out_2(SX_out_2));
  _16add u_16add_1 (.sub(1'b0), .in_2(plus_1_out_4), .in_3(SX_out_2), .out_4(n16add_1_out_4));  // open: cOUt, ovf
  Multiplexer #(.width(16), .enable("false")) multiplexer_7 (
    .in0(regfile_1_rt), .in1(SX_out_2), .out(multiplexer_7_out), .sel(CONTROL_rt_imm));
  and and_1 (and_1_out, alu_1_eqz, CONTROL_beqz);
  ALU alu_1 (
    .rs(regfile_1_rs), .rt(multiplexer_7_out), .outputdata(alu_1_outputdata), .shamt(rom_1_data),
    .opCode(rom_1_data_3[15:12]), .eqz(alu_1_eqz), .gt(alu_1_gt));
  Multiplexer #(.width(16)) multiplexer_8 (
    .in0(plus_1_out_4), .in1(n16add_1_out_4), .out(multiplexer_8_out), .sel(or_1_out));  // open: en
  or or_1 (or_1_out, and_1_out, and_2_out);
  and and_2 (and_2_out, CONTROL_bgt, alu_1_gt);
  not not_2 (not_2_out, clock_1_out);
  top4PC top4pc_1 (
    .imm({rom_1_data_4, rom_1_data_3[8:6], rom_1_data_2, rom_1_data}), .PC(PC_out[15:12]),
    .newPC(top4pc_1_newpc));
  RAM #(.addrWidth(16), .dataWidth(16), .bus("separate")) ram_1 (
    .addr(alu_1_outputdata), .din(regfile_1_rt), .data(ram_1_data), .str(CONTROL_sw), .clk(not_2_out));  // open: sel, ld, clr
  Multiplexer #(.width(16)) multiplexer_9 (
    .in0(multiplexer_8_out), .in1(top4pc_1_newpc), .out(multiplexer_9_out), .sel(CONTROL_j_jal));  // open: en
  Multiplexer #(.width(16), .enable("false")) multiplexer_10 (
    .in0(alu_1_outputdata), .in1(ram_1_data), .out(multiplexer_10_out), .sel(CONTROL_dm_alu));
  TTY #(.rows(13), .cols(80)) tty_1 (.data(alu_1_outputdata[6:0]), .clk(not_2_out), .we(CONTROL_output), .clr(reset));
  Multiplexer #(.width(16)) multiplexer_11 (
    .in0(multiplexer_9_out), .in1(alu_1_outputdata), .out(multiplexer_11_out), .sel(CONTROL_jr));  // open: en

  // Notes on the sheet:
  //   contents of rom_1 (hex, n*v repeats v):
  //   2100 2903 f008 22a0 e400 293f 8801 b002 803f
endmodule

module ALU (
  input  [15:0] rs,
  input  [15:0] rt,
  input  [3:0] opCode,
  input  [2:0] shamt,
  output [15:0] outputdata,
  output eqz,
  output gt
);

  wire not_1_out, not_2_out, not_3_out, not_4_out, not_5_out, not_6_out, not_7_out, not_8_out, not_9_out,
       not_10_out, not_11_out, not_12_out, not_13_out, not_14_out, not_15_out, not_16_out, not_17_out,
       not_18_out, or_1_out;
  wire [15:0] n16add_1_out_4, nand_out, shiftleft_1_out_3, shiftright_1_out_3, sub_2_out_4, sub_3_out_4,
       sub_4_out_4, sub_out_4, xor_out;

  _16add u_16add_1 (.sub(1'b0), .in_2(rs), .in_3(rt), .out_4(n16add_1_out_4));  // open: cOUt, ovf
  _16add sub (.sub(1'b1), .in_2(rs), .in_3(rt), .out_4(sub_out_4));  // open: cOUt, ovf
  _16add sub_2 (.sub(1'b1), .in_2(rs), .in_3({16{1'b0}}), .out_4(sub_2_out_4));  // open: cOUt, ovf
  _16add sub_3 (.sub(1'b1), .in_2(rs), .in_3(rt), .out_4(sub_3_out_4));  // open: cOUt, ovf
  assign xor_out = rs ^ rt;  // XOR_Gate xor, 16 bits wide
  assign nand_out = ~(rs & rt);  // NAND_Gate nand, 16 bits wide
  shiftright shiftright_1 (.in_1(rs), .shamt(shamt), .out_3(shiftright_1_out_3));
  shiftleft shiftleft_1 (.in_1(rs), .in_2(shamt), .out_3(shiftleft_1_out_3));
  not not_1 (not_1_out, sub_2_out_4[0]);
  not not_2 (not_2_out, sub_2_out_4[1]);
  not not_3 (not_3_out, sub_2_out_4[2]);
  not not_4 (not_4_out, sub_2_out_4[3]);
  not not_5 (not_5_out, sub_2_out_4[4]);
  not not_6 (not_6_out, sub_2_out_4[5]);
  not not_7 (not_7_out, sub_2_out_4[6]);
  not not_8 (not_8_out, sub_2_out_4[7]);
  not not_9 (not_9_out, sub_2_out_4[8]);
  not not_10 (not_10_out, sub_2_out_4[9]);
  not not_11 (not_11_out, sub_2_out_4[10]);
  not not_12 (not_12_out, sub_2_out_4[11]);
  not not_13 (not_13_out, sub_2_out_4[12]);
  not not_14 (not_14_out, sub_2_out_4[13]);
  not not_15 (not_15_out, sub_2_out_4[14]);
  not not_16 (not_16_out, sub_2_out_4[15]);
  _16add sub_4 (.sub(1'b1), .in_2(sub_3_out_4), .in_3({16{1'b0}}), .out_4(sub_4_out_4));  // open: cOUt, ovf
  and and_1 (eqz, not_1_out, not_2_out, not_3_out, not_4_out, not_5_out, not_6_out, not_7_out, not_8_out, not_9_out, not_10_out, not_11_out, not_12_out, not_13_out, not_14_out, not_15_out, not_16_out);
  or or_1 (or_1_out, sub_4_out_4[0], sub_4_out_4[1], sub_4_out_4[2], sub_4_out_4[3], sub_4_out_4[4], sub_4_out_4[5], sub_4_out_4[6], sub_4_out_4[7], sub_4_out_4[8], sub_4_out_4[9], sub_4_out_4[10], sub_4_out_4[11], sub_4_out_4[12], sub_4_out_4[13], sub_4_out_4[14]);
  and and_2 (gt, or_1_out, not_17_out, not_18_out);
  not not_17 (not_17_out, sub_4_out_4[15]);
  not not_18 (not_18_out, rs[15]);
  Multiplexer #(.select(4), .width(16)) multiplexer_1 (
    .in0(nand_out), .in1(xor_out), .in2(n16add_1_out_4), .in3(n16add_1_out_4), .in4(sub_out_4),
    .in5(shiftright_1_out_3), .in6(shiftleft_1_out_3), .in7(sub_out_4), .in8(sub_out_4),
    .in9(n16add_1_out_4), .in10(n16add_1_out_4), .in11(rs), .in12(rs), .in13(rs), .in14(rs), .in15(rs),
    .out(outputdata), .sel(opCode));  // open: en
endmodule

module _16bitregister (
  input  reset_input,
  input  write_enable,
  input  clock,
  input  [15:0] in,
  output [15:0] out
);

  D_Flip_Flop d_ff_1 (.clk(clock), .D(in[0]), .Q(out[0]), .en(write_enable), .reset(reset_input));  // open: Qn, preset
  D_Flip_Flop d_ff_2 (.clk(clock), .D(in[2]), .Q(out[2]), .en(write_enable), .reset(reset_input));  // open: Qn, preset
  D_Flip_Flop d_ff_3 (.clk(clock), .D(in[4]), .Q(out[4]), .en(write_enable), .reset(reset_input));  // open: Qn, preset
  D_Flip_Flop d_ff_4 (.clk(clock), .D(in[6]), .Q(out[6]), .en(write_enable), .reset(reset_input));  // open: Qn, preset
  D_Flip_Flop d_ff_5 (.clk(clock), .D(in[8]), .Q(out[8]), .en(write_enable), .reset(reset_input));  // open: Qn, preset
  D_Flip_Flop d_ff_6 (
    .clk(clock), .D(in[10]), .Q(out[10]), .en(write_enable), .reset(reset_input));  // open: Qn, preset
  D_Flip_Flop d_ff_7 (
    .clk(clock), .D(in[12]), .Q(out[12]), .en(write_enable), .reset(reset_input));  // open: Qn, preset
  D_Flip_Flop d_ff_8 (
    .clk(clock), .D(in[14]), .Q(out[14]), .en(write_enable), .reset(reset_input));  // open: Qn, preset
  D_Flip_Flop d_ff_9 (.clk(clock), .D(in[1]), .Q(out[1]), .en(write_enable), .reset(reset_input));  // open: Qn, preset
  D_Flip_Flop d_ff_10 (.clk(clock), .D(in[3]), .Q(out[3]), .en(write_enable), .reset(reset_input));  // open: Qn, preset
  D_Flip_Flop d_ff_11 (.clk(clock), .D(in[5]), .Q(out[5]), .en(write_enable), .reset(reset_input));  // open: Qn, preset
  D_Flip_Flop d_ff_12 (.clk(clock), .D(in[7]), .Q(out[7]), .en(write_enable), .reset(reset_input));  // open: Qn, preset
  D_Flip_Flop d_ff_13 (.clk(clock), .D(in[9]), .Q(out[9]), .en(write_enable), .reset(reset_input));  // open: Qn, preset
  D_Flip_Flop d_ff_14 (
    .clk(clock), .D(in[11]), .Q(out[11]), .en(write_enable), .reset(reset_input));  // open: Qn, preset
  D_Flip_Flop d_ff_15 (
    .clk(clock), .D(in[13]), .Q(out[13]), .en(write_enable), .reset(reset_input));  // open: Qn, preset
  D_Flip_Flop d_ff_16 (
    .clk(clock), .D(in[15]), .Q(out[15]), .en(write_enable), .reset(reset_input));  // open: Qn, preset
endmodule

module _1add (
  input  cIn,
  input  sub,
  input  A,
  input  B,
  output sum,
  output cOut
);

  wire and_1_out, and_2_out, xor_1_out, xor_2_out;

  xor xor_1 (xor_1_out, sub, B);
  and and_1 (and_1_out, A, xor_1_out);
  xor xor_2 (xor_2_out, A, xor_1_out);
  or or_1 (cOut, and_1_out, and_2_out);
  and and_2 (and_2_out, xor_2_out, cIn);
  xor xor_3 (sum, cIn, xor_2_out);
endmodule

module _4add (
  input  sub,
  input  cIn,
  input  [3:0] A,
  input  [3:0] B,
  output [3:0] result,
  output cOUT,
  output ovf
);

  wire n1add_1_cout, n1add_2_cout, n1add_3_cout;

  _1add u_1add_1 (.sub(sub), .A(A[0]), .B(B[0]), .cIn(cIn), .cOut(n1add_1_cout), .sum(result[0]));
  _1add u_1add_2 (.sub(sub), .A(A[1]), .B(B[1]), .cIn(n1add_1_cout), .cOut(n1add_2_cout), .sum(result[1]));
  _1add u_1add_3 (.sub(sub), .A(A[2]), .B(B[2]), .cIn(n1add_2_cout), .cOut(n1add_3_cout), .sum(result[2]));
  _1add u_1add_4 (.sub(sub), .A(A[3]), .B(B[3]), .cIn(n1add_3_cout), .cOut(cOUT), .sum(result[3]));
  xor xor_1 (ovf, cOUT, n1add_3_cout);
endmodule

module _16add (
  input  sub,
  input  [15:0] in_2,
  input  [15:0] in_3,
  output [15:0] out_4,
  output cOUt,
  output ovf
);

  wire n4add_1_cout, n4add_2_cout, n4add_3_cout;

  _4add u_4add_1 (
    .sub(sub), .A(in_2[3:0]), .B(in_3[3:0]), .cIn(sub), .cOUT(n4add_1_cout), .result(out_4[3:0]));  // open: ovf
  _4add u_4add_2 (
    .sub(sub), .A(in_2[7:4]), .B(in_3[7:4]), .cIn(n4add_1_cout), .cOUT(n4add_2_cout), .result(out_4[7:4]));  // open: ovf
  _4add u_4add_3 (
    .sub(sub), .A(in_2[11:8]), .B(in_3[11:8]), .cIn(n4add_2_cout), .cOUT(n4add_3_cout), .result(out_4[11:8]));  // open: ovf
  _4add u_4add_4 (
    .sub(sub), .A(in_2[15:12]), .B(in_3[15:12]), .cIn(n4add_3_cout), .cOUT(cOUt), .ovf(ovf),
    .result(out_4[15:12]));
endmodule

// shra
module shiftright (
  input  [15:0] in_1,
  input  [2:0] shamt,
  output [15:0] out_3
);

  wire multiplexer_1_out, multiplexer_2_out, multiplexer_3_out, multiplexer_4_out, multiplexer_5_out,
       multiplexer_6_out, multiplexer_7_out, multiplexer_8_out, multiplexer_9_out, multiplexer_10_out,
       multiplexer_11_out, multiplexer_12_out, multiplexer_13_out, multiplexer_14_out, multiplexer_15_out,
       multiplexer_16_out, multiplexer_17_out, multiplexer_21_out, multiplexer_22_out, multiplexer_23_out,
       multiplexer_24_out, multiplexer_25_out, multiplexer_29_out, multiplexer_30_out, multiplexer_31_out,
       multiplexer_32_out, multiplexer_33_out, multiplexer_34_out, multiplexer_37_out, multiplexer_38_out,
       multiplexer_39_out, multiplexer_43_out;

  Multiplexer multiplexer_1 (.in0(in_1[0]), .in1(in_1[1]), .out(multiplexer_1_out), .sel(shamt[0]));  // open: en
  Multiplexer multiplexer_2 (.in0(in_1[1]), .in1(in_1[2]), .out(multiplexer_2_out), .sel(shamt[0]));  // open: en
  Multiplexer multiplexer_3 (
    .in0(multiplexer_1_out), .in1(multiplexer_4_out), .out(multiplexer_3_out), .sel(shamt[1]));  // open: en
  Multiplexer multiplexer_4 (.in0(in_1[2]), .in1(in_1[3]), .out(multiplexer_4_out), .sel(shamt[0]));  // open: en
  Multiplexer multiplexer_5 (.in0(in_1[3]), .in1(in_1[4]), .out(multiplexer_5_out), .sel(shamt[0]));  // open: en
  Multiplexer multiplexer_6 (.in0(in_1[4]), .in1(in_1[5]), .out(multiplexer_6_out), .sel(shamt[0]));  // open: en
  Multiplexer multiplexer_7 (
    .in0(multiplexer_2_out), .in1(multiplexer_5_out), .out(multiplexer_7_out), .sel(shamt[1]));  // open: en
  Multiplexer multiplexer_8 (
    .in0(multiplexer_4_out), .in1(multiplexer_6_out), .out(multiplexer_8_out), .sel(shamt[1]));  // open: en
  Multiplexer multiplexer_9 (
    .in0(multiplexer_5_out), .in1(multiplexer_10_out), .out(multiplexer_9_out), .sel(shamt[1]));  // open: en
  Multiplexer multiplexer_10 (.in0(in_1[5]), .in1(in_1[6]), .out(multiplexer_10_out), .sel(shamt[0]));  // open: en
  Multiplexer multiplexer_11 (.in0(in_1[6]), .in1(in_1[7]), .out(multiplexer_11_out), .sel(shamt[0]));  // open: en
  Multiplexer multiplexer_12 (.in0(in_1[7]), .in1(in_1[8]), .out(multiplexer_12_out), .sel(shamt[0]));  // open: en
  Multiplexer multiplexer_13 (
    .in0(multiplexer_6_out), .in1(multiplexer_11_out), .out(multiplexer_13_out), .sel(shamt[1]));  // open: en
  Multiplexer multiplexer_14 (
    .in0(multiplexer_10_out), .in1(multiplexer_12_out), .out(multiplexer_14_out), .sel(shamt[1]));  // open: en
  Multiplexer multiplexer_15 (
    .in0(multiplexer_11_out), .in1(multiplexer_16_out), .out(multiplexer_15_out), .sel(shamt[1]));  // open: en
  Multiplexer multiplexer_16 (.in0(in_1[8]), .in1(in_1[9]), .out(multiplexer_16_out), .sel(shamt[0]));  // open: en
  Multiplexer multiplexer_17 (.in0(in_1[9]), .in1(in_1[10]), .out(multiplexer_17_out), .sel(shamt[0]));  // open: en
  Multiplexer multiplexer_18 (
    .in0(multiplexer_3_out), .in1(multiplexer_13_out), .out(out_3[0]), .sel(shamt[2]));  // open: en
  Multiplexer multiplexer_19 (
    .in0(multiplexer_7_out), .in1(multiplexer_14_out), .out(out_3[1]), .sel(shamt[2]));  // open: en
  Multiplexer multiplexer_20 (
    .in0(multiplexer_8_out), .in1(multiplexer_15_out), .out(out_3[2]), .sel(shamt[2]));  // open: en
  Multiplexer multiplexer_21 (
    .in0(multiplexer_12_out), .in1(multiplexer_17_out), .out(multiplexer_21_out), .sel(shamt[1]));  // open: en
  Multiplexer multiplexer_22 (
    .in0(multiplexer_16_out), .in1(multiplexer_23_out), .out(multiplexer_22_out), .sel(shamt[1]));  // open: en
  Multiplexer multiplexer_23 (.in0(in_1[10]), .in1(in_1[11]), .out(multiplexer_23_out), .sel(shamt[0]));  // open: en
  Multiplexer multiplexer_24 (.in0(in_1[11]), .in1(in_1[12]), .out(multiplexer_24_out), .sel(shamt[0]));  // open: en
  Multiplexer multiplexer_25 (.in0(in_1[12]), .in1(in_1[13]), .out(multiplexer_25_out), .sel(shamt[0]));  // open: en
  Multiplexer multiplexer_26 (
    .in0(multiplexer_9_out), .in1(multiplexer_21_out), .out(out_3[3]), .sel(shamt[2]));  // open: en
  Multiplexer multiplexer_27 (
    .in0(multiplexer_13_out), .in1(multiplexer_22_out), .out(out_3[4]), .sel(shamt[2]));  // open: en
  Multiplexer multiplexer_28 (
    .in0(multiplexer_14_out), .in1(multiplexer_29_out), .out(out_3[5]), .sel(shamt[2]));  // open: en
  Multiplexer multiplexer_29 (
    .in0(multiplexer_17_out), .in1(multiplexer_24_out), .out(multiplexer_29_out), .sel(shamt[1]));  // open: en
  Multiplexer multiplexer_30 (
    .in0(multiplexer_23_out), .in1(multiplexer_25_out), .out(multiplexer_30_out), .sel(shamt[1]));  // open: en
  Multiplexer multiplexer_31 (
    .in0(multiplexer_24_out), .in1(multiplexer_32_out), .out(multiplexer_31_out), .sel(shamt[1]));  // open: en
  Multiplexer multiplexer_32 (.in0(in_1[13]), .in1(in_1[14]), .out(multiplexer_32_out), .sel(shamt[0]));  // open: en
  Multiplexer multiplexer_33 (.in0(in_1[14]), .in1(in_1[15]), .out(multiplexer_33_out), .sel(shamt[0]));  // open: en
  Multiplexer multiplexer_34 (.in0(in_1[15]), .in1(in_1[15]), .out(multiplexer_34_out), .sel(shamt[0]));  // open: en
  Multiplexer multiplexer_35 (
    .in0(multiplexer_15_out), .in1(multiplexer_30_out), .out(out_3[6]), .sel(shamt[2]));  // open: en
  Multiplexer multiplexer_36 (
    .in0(multiplexer_21_out), .in1(multiplexer_31_out), .out(out_3[7]), .sel(shamt[2]));  // open: en
  Multiplexer multiplexer_37 (
    .in0(multiplexer_25_out), .in1(multiplexer_33_out), .out(multiplexer_37_out), .sel(shamt[1]));  // open: en
  Multiplexer multiplexer_38 (
    .in0(multiplexer_32_out), .in1(multiplexer_34_out), .out(multiplexer_38_out), .sel(shamt[1]));  // open: en
  Multiplexer multiplexer_39 (
    .in0(multiplexer_33_out), .in1(in_1[15]), .out(multiplexer_39_out), .sel(shamt[1]));  // open: en
  Multiplexer multiplexer_40 (
    .in0(multiplexer_22_out), .in1(multiplexer_37_out), .out(out_3[8]), .sel(shamt[2]));  // open: en
  Multiplexer multiplexer_41 (
    .in0(multiplexer_29_out), .in1(multiplexer_38_out), .out(out_3[9]), .sel(shamt[2]));  // open: en
  Multiplexer multiplexer_42 (
    .in0(multiplexer_30_out), .in1(multiplexer_39_out), .out(out_3[10]), .sel(shamt[2]));  // open: en
  Multiplexer multiplexer_43 (
    .in0(multiplexer_34_out), .in1(in_1[15]), .out(multiplexer_43_out), .sel(shamt[1]));  // open: en
  Multiplexer multiplexer_44 (
    .in0(multiplexer_31_out), .in1(multiplexer_43_out), .out(out_3[11]), .sel(shamt[2]));  // open: en
  Multiplexer multiplexer_45 (.in0(multiplexer_37_out), .in1(in_1[15]), .out(out_3[12]), .sel(shamt[2]));  // open: en
  Multiplexer multiplexer_46 (.in0(multiplexer_38_out), .in1(in_1[15]), .out(out_3[13]), .sel(shamt[2]));  // open: en
  Multiplexer multiplexer_47 (.in0(multiplexer_39_out), .in1(in_1[15]), .out(out_3[14]), .sel(shamt[2]));  // open: en
  Multiplexer multiplexer_48 (.in0(multiplexer_43_out), .in1(in_1[15]), .out(out_3[15]), .sel(shamt[2]));  // open: en
endmodule

// shl
module shiftleft (
  input  [15:0] in_1,
  input  [2:0] in_2,
  output [15:0] out_3
);

  wire multiplexer_1_out, multiplexer_2_out, multiplexer_3_out, multiplexer_4_out, multiplexer_5_out,
       multiplexer_6_out, multiplexer_7_out, multiplexer_8_out, multiplexer_9_out, multiplexer_10_out,
       multiplexer_11_out, multiplexer_12_out, multiplexer_13_out, multiplexer_14_out, multiplexer_15_out,
       multiplexer_16_out, multiplexer_19_out, multiplexer_20_out, multiplexer_21_out, multiplexer_22_out,
       multiplexer_23_out, multiplexer_27_out, multiplexer_28_out, multiplexer_29_out, multiplexer_30_out,
       multiplexer_31_out, multiplexer_35_out, multiplexer_36_out, multiplexer_37_out, multiplexer_38_out,
       multiplexer_41_out, multiplexer_42_out;

  Multiplexer multiplexer_1 (.in0(in_1[15]), .in1(in_1[14]), .out(multiplexer_1_out), .sel(in_2[0]));  // open: en
  Multiplexer multiplexer_2 (.in0(in_1[14]), .in1(in_1[13]), .out(multiplexer_2_out), .sel(in_2[0]));  // open: en
  Multiplexer multiplexer_3 (
    .in0(multiplexer_1_out), .in1(multiplexer_4_out), .out(multiplexer_3_out), .sel(in_2[1]));  // open: en
  Multiplexer multiplexer_4 (.in0(in_1[13]), .in1(in_1[12]), .out(multiplexer_4_out), .sel(in_2[0]));  // open: en
  Multiplexer multiplexer_5 (.in0(in_1[12]), .in1(in_1[11]), .out(multiplexer_5_out), .sel(in_2[0]));  // open: en
  Multiplexer multiplexer_6 (
    .in0(multiplexer_2_out), .in1(multiplexer_5_out), .out(multiplexer_6_out), .sel(in_2[1]));  // open: en
  Multiplexer multiplexer_7 (
    .in0(multiplexer_4_out), .in1(multiplexer_8_out), .out(multiplexer_7_out), .sel(in_2[1]));  // open: en
  Multiplexer multiplexer_8 (.in0(in_1[11]), .in1(in_1[10]), .out(multiplexer_8_out), .sel(in_2[0]));  // open: en
  Multiplexer multiplexer_9 (.in0(in_1[10]), .in1(in_1[9]), .out(multiplexer_9_out), .sel(in_2[0]));  // open: en
  Multiplexer multiplexer_10 (.in0(in_1[9]), .in1(in_1[8]), .out(multiplexer_10_out), .sel(in_2[0]));  // open: en
  Multiplexer multiplexer_11 (
    .in0(multiplexer_5_out), .in1(multiplexer_9_out), .out(multiplexer_11_out), .sel(in_2[1]));  // open: en
  Multiplexer multiplexer_12 (
    .in0(multiplexer_8_out), .in1(multiplexer_10_out), .out(multiplexer_12_out), .sel(in_2[1]));  // open: en
  Multiplexer multiplexer_13 (
    .in0(multiplexer_9_out), .in1(multiplexer_14_out), .out(multiplexer_13_out), .sel(in_2[1]));  // open: en
  Multiplexer multiplexer_14 (.in0(in_1[8]), .in1(in_1[7]), .out(multiplexer_14_out), .sel(in_2[0]));  // open: en
  Multiplexer multiplexer_15 (.in0(in_1[7]), .in1(in_1[6]), .out(multiplexer_15_out), .sel(in_2[0]));  // open: en
  Multiplexer multiplexer_16 (.in0(in_1[6]), .in1(in_1[5]), .out(multiplexer_16_out), .sel(in_2[0]));  // open: en
  Multiplexer multiplexer_17 (
    .in0(multiplexer_3_out), .in1(multiplexer_12_out), .out(out_3[15]), .sel(in_2[2]));  // open: en
  Multiplexer multiplexer_18 (
    .in0(multiplexer_6_out), .in1(multiplexer_13_out), .out(out_3[14]), .sel(in_2[2]));  // open: en
  Multiplexer multiplexer_19 (
    .in0(multiplexer_10_out), .in1(multiplexer_15_out), .out(multiplexer_19_out), .sel(in_2[1]));  // open: en
  Multiplexer multiplexer_20 (
    .in0(multiplexer_14_out), .in1(multiplexer_16_out), .out(multiplexer_20_out), .sel(in_2[1]));  // open: en
  Multiplexer multiplexer_21 (
    .in0(multiplexer_15_out), .in1(multiplexer_22_out), .out(multiplexer_21_out), .sel(in_2[1]));  // open: en
  Multiplexer multiplexer_22 (.in0(in_1[5]), .in1(in_1[4]), .out(multiplexer_22_out), .sel(in_2[0]));  // open: en
  Multiplexer multiplexer_23 (.in0(in_1[4]), .in1(in_1[3]), .out(multiplexer_23_out), .sel(in_2[0]));  // open: en
  Multiplexer multiplexer_24 (
    .in0(multiplexer_7_out), .in1(multiplexer_19_out), .out(out_3[13]), .sel(in_2[2]));  // open: en
  Multiplexer multiplexer_25 (
    .in0(multiplexer_11_out), .in1(multiplexer_20_out), .out(out_3[12]), .sel(in_2[2]));  // open: en
  Multiplexer multiplexer_26 (
    .in0(multiplexer_12_out), .in1(multiplexer_21_out), .out(out_3[11]), .sel(in_2[2]));  // open: en
  Multiplexer multiplexer_27 (
    .in0(multiplexer_16_out), .in1(multiplexer_23_out), .out(multiplexer_27_out), .sel(in_2[1]));  // open: en
  Multiplexer multiplexer_28 (
    .in0(multiplexer_22_out), .in1(multiplexer_29_out), .out(multiplexer_28_out), .sel(in_2[1]));  // open: en
  Multiplexer multiplexer_29 (.in0(in_1[3]), .in1(in_1[2]), .out(multiplexer_29_out), .sel(in_2[0]));  // open: en
  Multiplexer multiplexer_30 (.in0(in_1[2]), .in1(in_1[1]), .out(multiplexer_30_out), .sel(in_2[0]));  // open: en
  Multiplexer multiplexer_31 (.in0(in_1[1]), .in1(in_1[0]), .out(multiplexer_31_out), .sel(in_2[0]));  // open: en
  Multiplexer multiplexer_32 (
    .in0(multiplexer_13_out), .in1(multiplexer_27_out), .out(out_3[10]), .sel(in_2[2]));  // open: en
  Multiplexer multiplexer_33 (
    .in0(multiplexer_19_out), .in1(multiplexer_28_out), .out(out_3[9]), .sel(in_2[2]));  // open: en
  Multiplexer multiplexer_34 (
    .in0(multiplexer_20_out), .in1(multiplexer_35_out), .out(out_3[8]), .sel(in_2[2]));  // open: en
  Multiplexer multiplexer_35 (
    .in0(multiplexer_23_out), .in1(multiplexer_30_out), .out(multiplexer_35_out), .sel(in_2[1]));  // open: en
  Multiplexer multiplexer_36 (
    .in0(multiplexer_29_out), .in1(multiplexer_31_out), .out(multiplexer_36_out), .sel(in_2[1]));  // open: en
  Multiplexer multiplexer_37 (
    .in0(multiplexer_30_out), .in1(multiplexer_38_out), .out(multiplexer_37_out), .sel(in_2[1]));  // open: en
  Multiplexer multiplexer_38 (.in0(in_1[0]), .in1(1'b0), .out(multiplexer_38_out), .sel(in_2[0]));  // open: en
  Multiplexer multiplexer_39 (
    .in0(multiplexer_21_out), .in1(multiplexer_36_out), .out(out_3[7]), .sel(in_2[2]));  // open: en
  Multiplexer multiplexer_40 (
    .in0(multiplexer_27_out), .in1(multiplexer_37_out), .out(out_3[6]), .sel(in_2[2]));  // open: en
  Multiplexer multiplexer_41 (
    .in0(multiplexer_31_out), .in1(1'b0), .out(multiplexer_41_out), .sel(in_2[1]));  // open: en
  Multiplexer multiplexer_42 (
    .in0(multiplexer_38_out), .in1(1'b0), .out(multiplexer_42_out), .sel(in_2[1]));  // open: en
  Multiplexer multiplexer_43 (
    .in0(multiplexer_28_out), .in1(multiplexer_41_out), .out(out_3[5]), .sel(in_2[2]));  // open: en
  Multiplexer multiplexer_44 (
    .in0(multiplexer_35_out), .in1(multiplexer_42_out), .out(out_3[4]), .sel(in_2[2]));  // open: en
  Multiplexer multiplexer_45 (.in0(multiplexer_36_out), .in1(1'b0), .out(out_3[3]), .sel(in_2[2]));  // open: en
  Multiplexer multiplexer_46 (.in0(multiplexer_37_out), .in1(1'b0), .out(out_3[2]), .sel(in_2[2]));  // open: en
  Multiplexer multiplexer_47 (.in0(multiplexer_41_out), .in1(1'b0), .out(out_3[1]), .sel(in_2[2]));  // open: en
  Multiplexer multiplexer_48 (.in0(multiplexer_42_out), .in1(1'b0), .out(out_3[0]), .sel(in_2[2]));  // open: en
endmodule

module regfile (
  input  clock,
  input  global_reset,
  input  [2:0] rsReg,
  input  RegWriteEnable,
  input  [2:0] rdReg,
  input  [2:0] rtReg,
  input  [15:0] writeData,
  output [15:0] rs,
  output [15:0] rt
);

  wire and_1_out, and_2_out, and_3_out, and_4_out, and_5_out, and_6_out, and_7_out, decoder_1_out_3,
       decoder_1_out_4, decoder_1_out_5, decoder_1_out_6, decoder_1_out_7, decoder_1_out_8, decoder_1_out_9;
  wire [15:0] r0_out, r1_out, r2_out, r3_out, r4_out, r5_out, r6_out, r7_out;

  decoder decoder_1 (
    .in_1(rdReg), .out_3(decoder_1_out_3), .out_4(decoder_1_out_4), .out_5(decoder_1_out_5),
    .out_6(decoder_1_out_6), .out_7(decoder_1_out_7), .out_8(decoder_1_out_8), .out_9(decoder_1_out_9));  // open: out_2
  and and_1 (and_1_out, decoder_1_out_3, RegWriteEnable);
  and and_2 (and_2_out, decoder_1_out_4, RegWriteEnable);
  and and_3 (and_3_out, RegWriteEnable, decoder_1_out_5);
  and and_4 (and_4_out, RegWriteEnable, decoder_1_out_6);
  and and_5 (and_5_out, RegWriteEnable, decoder_1_out_7);
  and and_6 (and_6_out, RegWriteEnable, decoder_1_out_8);
  and and_7 (and_7_out, RegWriteEnable, decoder_1_out_9);
  _16bitregister r0 (.write_enable(1'b0), .clock(clock), .in(writeData), .reset_input(global_reset), .out(r0_out));
  _16bitregister r2 (.write_enable(and_2_out), .clock(clock), .in(writeData), .reset_input(global_reset), .out(r2_out));
  _16bitregister r4 (.write_enable(and_4_out), .clock(clock), .in(writeData), .reset_input(global_reset), .out(r4_out));
  _16bitregister r6 (.write_enable(and_6_out), .clock(clock), .in(writeData), .reset_input(global_reset), .out(r6_out));
  // Probe on r0_out
  // Probe on r2_out
  // Probe on r4_out
  // Probe on r6_out
  _16bitregister r1 (.write_enable(and_1_out), .clock(clock), .in(writeData), .reset_input(global_reset), .out(r1_out));
  _16bitregister r3 (.write_enable(and_3_out), .clock(clock), .in(writeData), .reset_input(global_reset), .out(r3_out));
  _16bitregister r5 (.write_enable(and_5_out), .clock(clock), .in(writeData), .reset_input(global_reset), .out(r5_out));
  _16bitregister r7 (.write_enable(and_7_out), .clock(clock), .in(writeData), .reset_input(global_reset), .out(r7_out));
  // Probe on r7_out
  // Probe on r1_out
  // Probe on r3_out
  // Probe on r5_out
  Multiplexer #(.select(3), .width(16)) multiplexer_1 (
    .in0(r0_out), .in1(r1_out), .in2(r2_out), .in3(r3_out), .in4(r4_out), .in5(r5_out), .in6(r6_out),
    .in7(r7_out), .out(rs), .sel(rsReg));  // open: en
  Multiplexer #(.select(3), .width(16)) multiplexer_2 (
    .in0(r0_out), .in1(r1_out), .in2(r2_out), .in3(r3_out), .in4(r4_out), .in5(r5_out), .in6(r6_out),
    .in7(r7_out), .out(rt), .sel(rtReg));  // open: en
endmodule

// Dcode
module decoder (
  input  [2:0] in_1,
  output out_2,
  output out_3,
  output out_4,
  output out_5,
  output out_6,
  output out_7,
  output out_8,
  output out_9
);

  wire not_1_out, not_2_out, not_3_out;

  not not_1 (not_1_out, in_1[0]);
  not not_2 (not_2_out, in_1[1]);
  not not_3 (not_3_out, in_1[2]);
  and and_1 (out_2, not_1_out, not_2_out, not_3_out);
  and and_2 (out_3, in_1[0], not_2_out, not_3_out);
  and and_3 (out_4, not_1_out, in_1[1], not_3_out);
  and and_4 (out_5, in_1[1], in_1[0], not_3_out);
  and and_5 (out_6, in_1[2], not_1_out, not_2_out);
  and and_6 (out_7, in_1[2], in_1[0], not_2_out);
  and and_7 (out_8, in_1[1], in_1[2], not_1_out);
  and and_8 (out_9, in_1[0], in_1[2], in_1[1]);
endmodule

module sign_extender (
  input  [5:0] in_1,
  output [15:0] out_2
);


  assign out_2 = {{11{in_1[5]}}, in_1[4:0]};
endmodule

module _1bitcomp (
  input  a,
  input  b,
  output a__b,
  output a_b
);

  wire and_1_out, and_2_out, not_1_out, not_2_out;

  not not_1 (not_1_out, a);
  not not_2 (not_2_out, b);
  and and_1 (and_1_out, not_1_out, b);
  and and_2 (and_2_out, b, a);
  and and_3 (a_b, a, not_2_out);
  or or_1 (a__b, and_1_out, and_2_out);
endmodule

module branchOP (
  input  [3:0] op,
  output beqz,
  output bgt
);

  wire not_1_out, not_2_out, not_3_out, not_4_out;

  not not_1 (not_1_out, op[0]);
  and and_1 (beqz, op[3], not_1_out, not_2_out, not_3_out);
  not not_2 (not_2_out, op[1]);
  not not_3 (not_3_out, op[2]);
  and and_2 (bgt, op[0], op[1], op[2], not_4_out);
  not not_4 (not_4_out, op[3]);
endmodule

module top4PC (
  input  [11:0] imm,
  input  [3:0] PC,
  output [15:0] newPC
);


  assign newPC = {PC, imm};
endmodule

module inputTo16 (
  input  [6:0] in_1,
  input  valid,
  output [15:0] out
);

  Multiplexer #(.width(16)) multiplexer_1 (.in0(16'h80), .in1({{9{1'b0}}, in_1}), .out(out), .sel(valid));  // open: en
endmodule

module Control (
  input  [3:0] opcode,
  output jal,
  output \input ,
  output WE,
  output rt_rd,
  output rt_imm,
  output beqz,
  output bgt,
  output sw,
  output j_jal,
  output jr,
  output DM_ALU,
  output \output 
);

  wire demultiplexer_1_out0, demultiplexer_1_out1, demultiplexer_1_out2, demultiplexer_1_out3,
       demultiplexer_1_out4, demultiplexer_1_out5, demultiplexer_1_out6, demultiplexer_1_out9,
       demultiplexer_1_out10, demultiplexer_1_out11, demultiplexer_1_out12, demultiplexer_1_out13,
       demultiplexer_1_out14, demultiplexer_1_out15;

  Demultiplexer #(.select(4)) demultiplexer_1 (
    .out0(demultiplexer_1_out0), .out1(demultiplexer_1_out1), .out2(demultiplexer_1_out2),
    .out3(demultiplexer_1_out3), .out4(demultiplexer_1_out4), .out5(demultiplexer_1_out5),
    .out6(demultiplexer_1_out6), .out7(bgt), .out8(beqz), .out9(demultiplexer_1_out9),
    .out10(demultiplexer_1_out10), .out11(demultiplexer_1_out11), .out12(demultiplexer_1_out12),
    .out13(demultiplexer_1_out13), .out14(demultiplexer_1_out14), .out15(demultiplexer_1_out15), .in(1'b1),
    .sel(opcode));  // open: en
  buf or_1 (jal, demultiplexer_1_out13);  // OR_Gate
  buf or_2 (\input , demultiplexer_1_out15);  // OR_Gate
  or or_3 (WE, demultiplexer_1_out0, demultiplexer_1_out1, demultiplexer_1_out2, demultiplexer_1_out3, demultiplexer_1_out4, demultiplexer_1_out5, demultiplexer_1_out6, demultiplexer_1_out9, demultiplexer_1_out13, demultiplexer_1_out15);
  or or_4 (rt_rd, demultiplexer_1_out2, demultiplexer_1_out9);
  or or_5 (rt_imm, demultiplexer_1_out2, demultiplexer_1_out9, demultiplexer_1_out10);
  buf or_6 (sw, demultiplexer_1_out10);  // OR_Gate
  or or_7 (j_jal, demultiplexer_1_out11, demultiplexer_1_out13);
  buf or_8 (jr, demultiplexer_1_out12);  // OR_Gate
  buf or_9 (DM_ALU, demultiplexer_1_out9);  // OR_Gate
  buf or_10 (\output , demultiplexer_1_out14);  // OR_Gate
endmodule

module \type  (
  input  [3:0] in_1,
  output out_2,
  output out_3,
  output out_4
);

  wire and_1_out, and_2_out, and_3_out, and_4_out, and_5_out, and_6_out, and_7_out, and_8_out, and_9_out,
       and_10_out, and_11_out, and_12_out, and_13_out, and_14_out, and_15_out, and_16_out, not_1_out,
       not_2_out, not_3_out, not_4_out;

  not not_1 (not_1_out, in_1[0]);
  not not_2 (not_2_out, in_1[1]);
  not not_3 (not_3_out, in_1[2]);
  not not_4 (not_4_out, in_1[3]);
  and and_1 (and_1_out, not_1_out, not_2_out, not_3_out, not_4_out);
  and and_2 (and_2_out, not_2_out, not_3_out, not_4_out, in_1[0]);
  and and_3 (and_3_out, not_1_out, not_3_out, not_4_out, in_1[1]);
  and and_4 (and_4_out, not_3_out, not_4_out, in_1[0], in_1[1]);
  and and_5 (and_5_out, not_1_out, not_2_out, not_4_out, in_1[2]);
  and and_6 (and_6_out, not_2_out, not_4_out, in_1[0], in_1[2]);
  and and_7 (and_7_out, not_1_out, not_4_out, in_1[1], in_1[2]);
  and and_8 (and_8_out, not_4_out, in_1[0], in_1[1], in_1[2]);
  and and_9 (and_9_out, not_1_out, not_2_out, not_3_out, in_1[3]);
  and and_10 (and_10_out, not_2_out, not_3_out, in_1[0], in_1[3]);
  and and_11 (and_11_out, not_1_out, not_3_out, in_1[1], in_1[3]);
  and and_12 (and_12_out, not_3_out, in_1[0], in_1[1], in_1[3]);
  and and_13 (and_13_out, not_1_out, not_2_out, in_1[2], in_1[3]);
  and and_14 (and_14_out, not_2_out, in_1[0], in_1[2], in_1[3]);
  and and_15 (and_15_out, not_1_out, in_1[1], in_1[2], in_1[3]);
  and and_16 (and_16_out, in_1[0], in_1[1], in_1[2], in_1[3]);
  or R (out_2, and_1_out, and_2_out, and_4_out, and_5_out, and_6_out, and_7_out, and_13_out, and_15_out, and_16_out);
  or I (out_3, and_3_out, and_10_out, and_11_out, and_9_out, and_8_out);
  or J (out_4, and_12_out, and_14_out);
endmodule
